# Fritzing sketch Untitled Sketch (saved by Fritzing 0.8.7b)
breadboards: 1

parts:
  U1 = LCD-16X2 [package=lcd-16x2]  # not connected
  R1 = Rotary Potentiometer (Small) [maximum_resistance=100kΩ package=THT]  # not connected
  R2 = Rotary Potentiometer (Small) [maximum_resistance=100kΩ package=THT]  # not connected
  J1 = Basic Servo
  Part1 = Arduino Uno (Rev3)

nets:
  N1: J1.pulse, Part1.D9_PWM
